// Logisim project 8bit_ALU.circ as structural Verilog: 1 circuit, main circuit main
module main (
  input  o0,
  input  o1,
  input  o2,
  input  a0,
  input  b0,
  input  a1,
  input  b1,
  input  a2,
  input  b2,
  input  a3,
  input  b3,
  input  a4,
  input  b4,
  input  a5,
  input  b5,
  input  a6,
  input  b6,
  input  a7,
  input  b7,
  output r0,
  output r1,
  output r2,
  output r3,
  output r4,
  output r5,
  output r6,
  output r7,
  output CARRY
);

  wire ADDSUB0_out, ADDSUB1_out, ADDSUB2_out, ADDSUB3_out, ADDSUB4_out, ADDSUB5_out, ADDSUB6_out,
       ADDSUB7_out, AND0_out, AND1_out, AND2_out, AND3_out, AND4_out, AND5_out, AND6_out, AND7_out,
       and_1_out, and_2_out, and_3_out, and_4_out, and_5_out, and_6_out, and_7_out, and_8_out, NOT0_out,
       NOT1_out, NOT2_out, NOT3_out, NOT4_out, NOT5_out, NOT6_out, NOT7_out, OR0_out, OR1_out, OR2_out,
       OR3_out, OR4_out, OR5_out, OR6_out, OR7_out, or_1_out, or_2_out, or_3_out, or_4_out, or_5_out,
       or_6_out, or_7_out, XOR0_out, XOR1_out, XOR2_out, XOR3_out, XOR4_out, XOR5_out, XOR6_out, XOR7_out;

  xor NOT0 (NOT0_out, b0, o1);
  or OR0 (OR0_out, a0, b0);
  xor NOT1 (NOT1_out, b1, o1);
  or OR1 (OR1_out, a1, b1);
  xor NOT2 (NOT2_out, b2, o1);
  or OR2 (OR2_out, a2, b2);
  xor NOT3 (NOT3_out, b3, o1);
  or OR3 (OR3_out, a3, b3);
  xor NOT4 (NOT4_out, b4, o1);
  or OR4 (OR4_out, a4, b4);
  xor NOT5 (NOT5_out, b5, o1);
  or OR5 (OR5_out, a5, b5);
  xor NOT6 (NOT6_out, b6, o1);
  or OR6 (OR6_out, a6, b6);
  xor NOT7 (NOT7_out, b7, o1);
  or OR7 (OR7_out, a7, b7);
  xor XOR0 (XOR0_out, a0, NOT0_out);
  and AND0 (AND0_out, a0, NOT0_out);
  xor XOR1 (XOR1_out, a1, NOT1_out);
  and AND1 (AND1_out, a1, NOT1_out);
  xor XOR2 (XOR2_out, a2, NOT2_out);
  and AND2 (AND2_out, a2, NOT2_out);
  xor XOR3 (XOR3_out, a3, NOT3_out);
  and AND3 (AND3_out, a3, NOT3_out);
  xor XOR4 (XOR4_out, a4, NOT4_out);
  and AND4 (AND4_out, a4, NOT4_out);
  xor XOR5 (XOR5_out, a5, NOT5_out);
  and AND5 (AND5_out, a5, NOT5_out);
  xor XOR6 (XOR6_out, a6, NOT6_out);
  and AND6 (AND6_out, a6, NOT6_out);
  xor XOR7 (XOR7_out, a7, NOT7_out);
  and AND7 (AND7_out, a7, NOT7_out);
  xor ADDSUB0 (ADDSUB0_out, XOR0_out, o1);
  and and_1 (and_1_out, XOR0_out, o1);
  xor ADDSUB1 (ADDSUB1_out, XOR1_out, or_1_out);
  and and_2 (and_2_out, XOR1_out, or_1_out);
  xor ADDSUB2 (ADDSUB2_out, XOR2_out, or_2_out);
  and and_3 (and_3_out, XOR2_out, or_2_out);
  xor ADDSUB3 (ADDSUB3_out, XOR3_out, or_3_out);
  and and_4 (and_4_out, XOR3_out, or_3_out);
  xor ADDSUB4 (ADDSUB4_out, XOR4_out, or_4_out);
  and and_5 (and_5_out, XOR4_out, or_4_out);
  xor ADDSUB5 (ADDSUB5_out, XOR5_out, or_5_out);
  and and_6 (and_6_out, XOR5_out, or_5_out);
  xor ADDSUB6 (ADDSUB6_out, XOR6_out, or_6_out);
  and and_7 (and_7_out, XOR6_out, or_6_out);
  xor ADDSUB7 (ADDSUB7_out, XOR7_out, or_7_out);
  and and_8 (and_8_out, XOR7_out, or_7_out);
  or or_1 (or_1_out, and_1_out, AND0_out);
  or or_2 (or_2_out, and_2_out, AND1_out);
  or or_3 (or_3_out, and_3_out, AND2_out);
  or or_4 (or_4_out, and_4_out, AND3_out);
  or or_5 (or_5_out, and_5_out, AND4_out);
  or or_6 (or_6_out, and_6_out, AND5_out);
  or or_7 (or_7_out, and_7_out, AND6_out);
  or or_8 (CARRY, and_8_out, AND7_out);
  Multiplexer #(.select(3)) multiplexer_1 (
    .in0(ADDSUB0_out), .in1(AND0_out), .in2(ADDSUB0_out), .in3(NOT0_out), .in4(XOR0_out), .in5(OR0_out),
    .in6(1'b0), .in7(b1), .out(r0), .sel({o2, o1, o0}));
  Multiplexer #(.select(3)) multiplexer_2 (
    .in0(ADDSUB1_out), .in1(AND1_out), .in2(ADDSUB1_out), .in3(NOT1_out), .in4(XOR1_out), .in5(OR1_out),
    .in6(b0), .in7(b2), .out(r1), .sel({o2, o1, o0}));
  Multiplexer #(.select(3)) multiplexer_3 (
    .in0(ADDSUB2_out), .in1(AND2_out), .in2(ADDSUB2_out), .in3(NOT2_out), .in4(XOR2_out), .in5(OR2_out),
    .in6(b1), .in7(b3), .out(r2), .sel({o2, o1, o0}));
  Multiplexer #(.select(3)) multiplexer_4 (
    .in0(ADDSUB3_out), .in1(AND3_out), .in2(ADDSUB3_out), .in3(NOT3_out), .in4(XOR3_out), .in5(OR3_out),
    .in6(b2), .in7(b4), .out(r3), .sel({o2, o1, o0}));
  Multiplexer #(.select(3)) multiplexer_5 (
    .in0(ADDSUB4_out), .in1(AND4_out), .in2(ADDSUB4_out), .in3(NOT4_out), .in4(XOR4_out), .in5(OR4_out),
    .in6(b3), .in7(b5), .out(r4), .sel({o2, o1, o0}));
  Multiplexer #(.select(3)) multiplexer_6 (
    .in0(ADDSUB5_out), .in1(AND5_out), .in2(ADDSUB5_out), .in3(NOT5_out), .in4(XOR5_out), .in5(OR5_out),
    .in6(b4), .in7(b6), .out(r5), .sel({o2, o1, o0}));
  Multiplexer #(.select(3)) multiplexer_7 (
    .in0(ADDSUB6_out), .in1(AND6_out), .in2(ADDSUB6_out), .in3(NOT6_out), .in4(XOR6_out), .in5(OR6_out),
    .in6(b5), .in7(b7), .out(r6), .sel({o2, o1, o0}));
  Multiplexer #(.select(3)) multiplexer_8 (
    .in0(ADDSUB7_out), .in1(AND7_out), .in2(ADDSUB7_out), .in3(NOT7_out), .in4(XOR7_out), .in5(OR7_out),
    .in6(b6), .in7(1'b0), .out(r7), .sel({o2, o1, o0}));
endmodule
