// Logisim project 8bit_adder.circ as structural Verilog: 1 circuit, main circuit main
module main (
  input  a0,
  input  b0,
  input  in_3,
  input  a1,
  input  b1,
  input  a2,
  input  b2,
  input  a3,
  input  b3,
  input  a4,
  input  b4,
  input  a5,
  input  b5,
  input  a6,
  input  b6,
  input  a7,
  input  b7,
  output sum0,
  output sum1,
  output sum2,
  output sum3,
  output sum4,
  output sum5,
  output sum6,
  output sum7,
  output carry
);

  wire and_1_out, and_2_out, and_3_out, and_4_out, and_5_out, and_6_out, and_7_out, and_8_out, and_9_out,
       and_10_out, and_11_out, and_12_out, and_13_out, and_14_out, and_15_out, and_16_out, or_1_out,
       or_2_out, or_3_out, or_4_out, or_5_out, or_6_out, or_7_out, xor_1_out, xor_2_out, xor_3_out,
       xor_4_out, xor_5_out, xor_6_out, xor_7_out, xor_8_out;

  xor xor_1 (xor_1_out, a0, b0);
  and and_1 (and_1_out, a0, b0);
  xor xor_2 (xor_2_out, a1, b1);
  and and_2 (and_2_out, a1, b1);
  xor xor_3 (xor_3_out, a2, b2);
  and and_3 (and_3_out, a2, b2);
  xor xor_4 (xor_4_out, a3, b3);
  and and_4 (and_4_out, a3, b3);
  xor xor_5 (xor_5_out, a4, b4);
  and and_5 (and_5_out, a4, b4);
  xor xor_6 (xor_6_out, a5, b5);
  and and_6 (and_6_out, a5, b5);
  xor xor_7 (xor_7_out, a6, b6);
  and and_7 (and_7_out, a6, b6);
  xor xor_8 (xor_8_out, a7, b7);
  and and_8 (and_8_out, a7, b7);
  xor xor_9 (sum0, xor_1_out, in_3);
  and and_9 (and_9_out, xor_1_out, in_3);
  xor xor_10 (sum1, xor_2_out, or_1_out);
  and and_10 (and_10_out, xor_2_out, or_1_out);
  xor xor_11 (sum2, xor_3_out, or_2_out);
  and and_11 (and_11_out, xor_3_out, or_2_out);
  xor xor_12 (sum3, xor_4_out, or_3_out);
  and and_12 (and_12_out, xor_4_out, or_3_out);
  xor xor_13 (sum4, xor_5_out, or_4_out);
  and and_13 (and_13_out, xor_5_out, or_4_out);
  xor xor_14 (sum5, xor_6_out, or_5_out);
  and and_14 (and_14_out, xor_6_out, or_5_out);
  xor xor_15 (sum6, xor_7_out, or_6_out);
  and and_15 (and_15_out, xor_7_out, or_6_out);
  xor xor_16 (sum7, xor_8_out, or_7_out);
  and and_16 (and_16_out, xor_8_out, or_7_out);
  or or_1 (or_1_out, and_9_out, and_1_out);
  or or_2 (or_2_out, and_10_out, and_2_out);
  or or_3 (or_3_out, and_11_out, and_3_out);
  or or_4 (or_4_out, and_12_out, and_4_out);
  or or_5 (or_5_out, and_13_out, and_5_out);
  or or_6 (or_6_out, and_14_out, and_6_out);
  or or_7 (or_7_out, and_15_out, and_7_out);
  or or_8 (carry, and_16_out, and_8_out);
endmodule
