// Logisim project 8bit_carry_lookahead_adder_demo.circ as structural Verilog: 1 circuit, main circuit main
module main (
  input  carry_in,
  input  a0,
  input  b0,
  input  a1,
  input  b1,
  input  a2,
  input  b2,
  input  a3,
  input  b3,
  input  a4,
  input  b4,
  input  a5,
  input  b5,
  input  a6,
  input  b6,
  input  a7,
  input  b7,
  output sum0,
  output sum1,
  output sum2,
  output sum3,
  output sum4,
  output sum5,
  output sum6,
  output sum7,
  output carry_out
);

  wire and_1_out, and_2_out, and_3_out, and_4_out, and_5_out, and_6_out, and_7_out, and_8_out, and_9_out,
       and_10_out, and_11_out, and_12_out, and_13_out, and_14_out, and_15_out, and_16_out, and_17_out,
       and_18_out, and_19_out, and_20_out, and_21_out, and_22_out, and_23_out, and_24_out, g0_out, g1_out,
       g2_out, g3_out, or_1_out, or_2_out, or_3_out, or_4_out, or_5_out, or_6_out, or_7_out, p0_out, p1_out,
       p2_out, p3_out, xor_1_out, xor_2_out, xor_3_out, xor_4_out;

  xor p0 (p0_out, a0, b0);
  and g0 (g0_out, a0, b0);
  xor p1 (p1_out, a1, b1);
  and g1 (g1_out, a1, b1);
  xor p2 (p2_out, a2, b2);
  and g2 (g2_out, a2, b2);
  xor p3 (p3_out, a3, b3);
  and g3 (g3_out, a3, b3);
  xor xor_1 (xor_1_out, a4, b4);
  and and_1 (and_1_out, a4, b4);
  xor xor_2 (xor_2_out, a5, b5);
  and and_2 (and_2_out, a5, b5);
  xor xor_3 (xor_3_out, a6, b6);
  and and_3 (and_3_out, a6, b6);
  xor xor_4 (xor_4_out, a7, b7);
  and and_4 (and_4_out, a7, b7);
  and and_5 (and_5_out, p0_out, carry_in);
  and and_6 (and_6_out, xor_1_out, or_7_out);
  xor xor_5 (sum0, p0_out, carry_in);
  or or_1 (or_1_out, g0_out, and_5_out);
  and and_7 (and_7_out, p1_out, and_5_out);
  xor xor_6 (sum4, xor_1_out, or_7_out);
  or or_2 (or_2_out, and_1_out, and_6_out);
  and and_8 (and_8_out, xor_2_out, and_6_out);
  xor xor_7 (sum1, p1_out, or_1_out);
  and and_9 (and_9_out, p1_out, g0_out);
  and and_10 (and_10_out, p2_out, and_7_out);
  xor xor_8 (sum5, xor_2_out, or_2_out);
  and and_11 (and_11_out, xor_2_out, and_1_out);
  and and_12 (and_12_out, xor_3_out, and_8_out);
  or or_3 (or_3_out, g1_out, and_9_out, and_7_out);
  and and_13 (and_13_out, p2_out, g1_out);
  and and_14 (and_14_out, p2_out, and_9_out);
  and and_15 (and_15_out, p3_out, and_14_out);
  and and_16 (and_16_out, p3_out, and_10_out);
  or or_4 (or_4_out, and_2_out, and_11_out, and_8_out);
  and and_17 (and_17_out, xor_3_out, and_2_out);
  and and_18 (and_18_out, xor_3_out, and_11_out);
  and and_19 (and_19_out, xor_4_out, and_18_out);
  and and_20 (and_20_out, xor_4_out, and_12_out);
  xor xor_9 (sum2, p2_out, or_3_out);
  or or_5 (or_5_out, g2_out, and_13_out, and_14_out, and_10_out);
  and and_21 (and_21_out, p3_out, g2_out);
  and and_22 (and_22_out, p3_out, and_13_out);
  xor xor_10 (sum6, xor_3_out, or_4_out);
  or or_6 (or_6_out, and_3_out, and_17_out, and_18_out, and_12_out);
  and and_23 (and_23_out, xor_4_out, and_3_out);
  and and_24 (and_24_out, xor_4_out, and_17_out);
  xor xor_11 (sum3, p3_out, or_5_out);
  xor xor_12 (sum7, xor_4_out, or_6_out);
  or or_7 (or_7_out, g3_out, and_21_out, and_22_out, and_15_out, and_16_out);
  or or_8 (carry_out, and_4_out, and_23_out, and_24_out, and_19_out, and_20_out);
endmodule
