// Logisim project 8bit_adder_with_subtraction.circ as structural Verilog: 1 circuit, main circuit main
module main (
  input  subtract,
  input  a0,
  input  b0,
  input  a1,
  input  b1,
  input  a2,
  input  b2,
  input  a3,
  input  b3,
  input  a4,
  input  b4,
  input  a5,
  input  b5,
  input  a6,
  input  b6,
  input  a7,
  input  b7,
  output sum0,
  output sum1,
  output sum2,
  output sum3,
  output sum4,
  output sum5,
  output sum6,
  output sum7,
  output carry
);

  wire and_1_out, and_2_out, and_3_out, and_4_out, and_5_out, and_6_out, and_7_out, and_8_out, and_9_out,
       and_10_out, and_11_out, and_12_out, and_13_out, and_14_out, and_15_out, and_16_out, or_1_out,
       or_2_out, or_3_out, or_4_out, or_5_out, or_6_out, or_7_out, xor_1_out, xor_2_out, xor_3_out,
       xor_4_out, xor_5_out, xor_6_out, xor_7_out, xor_8_out, xor_9_out, xor_10_out, xor_11_out, xor_12_out,
       xor_13_out, xor_14_out, xor_15_out, xor_16_out;

  xor xor_1 (xor_1_out, b0, subtract);
  xor xor_2 (xor_2_out, b1, subtract);
  xor xor_3 (xor_3_out, b2, subtract);
  xor xor_4 (xor_4_out, b3, subtract);
  xor xor_5 (xor_5_out, b4, subtract);
  xor xor_6 (xor_6_out, b5, subtract);
  xor xor_7 (xor_7_out, b6, subtract);
  xor xor_8 (xor_8_out, b7, subtract);
  xor xor_9 (xor_9_out, a0, xor_1_out);
  and and_1 (and_1_out, a0, xor_1_out);
  xor xor_10 (xor_10_out, a1, xor_2_out);
  and and_2 (and_2_out, a1, xor_2_out);
  xor xor_11 (xor_11_out, a2, xor_3_out);
  and and_3 (and_3_out, a2, xor_3_out);
  xor xor_12 (xor_12_out, a3, xor_4_out);
  and and_4 (and_4_out, a3, xor_4_out);
  xor xor_13 (xor_13_out, a4, xor_5_out);
  and and_5 (and_5_out, a4, xor_5_out);
  xor xor_14 (xor_14_out, a5, xor_6_out);
  and and_6 (and_6_out, a5, xor_6_out);
  xor xor_15 (xor_15_out, a6, xor_7_out);
  and and_7 (and_7_out, a6, xor_7_out);
  xor xor_16 (xor_16_out, a7, xor_8_out);
  and and_8 (and_8_out, a7, xor_8_out);
  xor xor_17 (sum0, xor_9_out, subtract);
  and and_9 (and_9_out, xor_9_out, subtract);
  xor xor_18 (sum1, xor_10_out, or_1_out);
  and and_10 (and_10_out, xor_10_out, or_1_out);
  xor xor_19 (sum2, xor_11_out, or_2_out);
  and and_11 (and_11_out, xor_11_out, or_2_out);
  xor xor_20 (sum3, xor_12_out, or_3_out);
  and and_12 (and_12_out, xor_12_out, or_3_out);
  xor xor_21 (sum4, xor_13_out, or_4_out);
  and and_13 (and_13_out, xor_13_out, or_4_out);
  xor xor_22 (sum5, xor_14_out, or_5_out);
  and and_14 (and_14_out, xor_14_out, or_5_out);
  xor xor_23 (sum6, xor_15_out, or_6_out);
  and and_15 (and_15_out, xor_15_out, or_6_out);
  xor xor_24 (sum7, xor_16_out, or_7_out);
  and and_16 (and_16_out, xor_16_out, or_7_out);
  or or_1 (or_1_out, and_9_out, and_1_out);
  or or_2 (or_2_out, and_10_out, and_2_out);
  or or_3 (or_3_out, and_11_out, and_3_out);
  or or_4 (or_4_out, and_12_out, and_4_out);
  or or_5 (or_5_out, and_13_out, and_5_out);
  or or_6 (or_6_out, and_14_out, and_6_out);
  or or_7 (or_7_out, and_15_out, and_7_out);
  or or_8 (carry, and_16_out, and_8_out);
endmodule
