// Logisim project 1bit_alu_demo.circ as structural Verilog: 1 circuit, main circuit main
module main (
  input  A,
  input  B,
  input  [2:0] in_3,
  output Y,
  output C_out
);

  wire adder_1_out, and_1_out, and_2_out, and_3_out, decoder_1_out0, decoder_1_out1, nand_1_out, nor_1_out,
       not_1_out, or_1_out, xor_1_out, xor_2_out;

  xor xor_1 (xor_1_out, B, in_3[0]);
  Adder #(.width(1)) adder_1 (.a(A), .b(xor_1_out), .out(adder_1_out), .cin(in_3[0]), .cout(C_out));
  Decoder #(.enable("false")) decoder_1 (.out0(decoder_1_out0), .out1(decoder_1_out1), .sel(in_3[0]));
  and and_1 (and_1_out, A, B);
  or or_1 (or_1_out, A, B);
  xor xor_2 (xor_2_out, A, B);
  nand nand_1 (nand_1_out, A, B);
  nor nor_1 (nor_1_out, A, B);
  and and_2 (and_2_out, decoder_1_out0, adder_1_out);
  and and_3 (and_3_out, adder_1_out, decoder_1_out1);
  not not_1 (not_1_out, A);
  Multiplexer #(.select(3)) multiplexer_1 (
    .in0(not_1_out), .in1(and_1_out), .in2(or_1_out), .in3(xor_2_out), .in4(nand_1_out), .in5(nor_1_out),
    .in6(and_2_out), .in7(and_3_out), .out(Y), .sel(in_3));
endmodule
