// Logisim project 8bit_ALU.circ as structural Verilog: 1 circuit, main circuit main
module main (
  input  subtract,
  input  a0,
  input  b0,
  input  a1,
  input  b1,
  input  a2,
  input  b2,
  input  a3,
  input  b3,
  input  a4,
  input  b4,
  input  a5,
  input  b5,
  input  a6,
  input  b6,
  input  a7,
  input  b7,
  output ADDSUB0,
  output XOR0,
  output NOT0,
  output AND0,
  output OR0,
  output SHL0,
  output SHR0,
  output ADDSUB1,
  output XOR1,
  output NOT1,
  output AND1,
  output OR1,
  output SHL1,
  output SHR1,
  output ADDSUB2,
  output XOR2,
  output NOT2,
  output AND2,
  output OR2,
  output SHL2,
  output SHR2,
  output ADDSUB3,
  output XOR3,
  output NOT3,
  output AND3,
  output OR3,
  output SHL3,
  output SHR3,
  output ADDSUB4,
  output XOR4,
  output NOT4,
  output AND4,
  output OR4,
  output SHL4,
  output SHR4,
  output ADDSUB5,
  output XOR5,
  output NOT5,
  output AND5,
  output OR5,
  output SHL5,
  output SHR5,
  output ADDSUB6,
  output XOR6,
  output NOT6,
  output AND6,
  output OR6,
  output SHL6,
  output SHR6,
  output ADDSUB7,
  output XOR7,
  output NOT7,
  output AND7,
  output OR7,
  output SHL7,
  output SHR7,
  output carry
);

  wire and_9_out, and_10_out, and_11_out, and_12_out, and_13_out, and_14_out, and_15_out, and_16_out,
       or_9_out, or_10_out, or_11_out, or_12_out, or_13_out, or_14_out, or_15_out;

  xor xor_1 (NOT0, b0, subtract);
  or or_1 (OR0, a0, b0);
  xor xor_2 (NOT1, b1, subtract);
  or or_2 (OR1, a1, b1);
  xor xor_3 (NOT2, b2, subtract);
  or or_3 (OR2, a2, b2);
  xor xor_4 (NOT3, b3, subtract);
  or or_4 (OR3, a3, b3);
  xor xor_5 (NOT4, b4, subtract);
  or or_5 (OR4, a4, b4);
  xor xor_6 (NOT5, b5, subtract);
  or or_6 (OR5, a5, b5);
  xor xor_7 (NOT6, b6, subtract);
  or or_7 (OR6, a6, b6);
  xor xor_8 (NOT7, b7, subtract);
  or or_8 (OR7, a7, b7);
  xor xor_9 (XOR0, a0, NOT0);
  and and_1 (AND0, a0, NOT0);
  xor xor_10 (XOR1, a1, NOT1);
  and and_2 (AND1, a1, NOT1);
  xor xor_11 (XOR2, a2, NOT2);
  and and_3 (AND2, a2, NOT2);
  xor xor_12 (XOR3, a3, NOT3);
  and and_4 (AND3, a3, NOT3);
  xor xor_13 (XOR4, a4, NOT4);
  and and_5 (AND4, a4, NOT4);
  xor xor_14 (XOR5, a5, NOT5);
  and and_6 (AND5, a5, NOT5);
  xor xor_15 (XOR6, a6, NOT6);
  and and_7 (AND6, a6, NOT6);
  xor xor_16 (XOR7, a7, NOT7);
  and and_8 (AND7, a7, NOT7);
  xor xor_17 (ADDSUB0, XOR0, subtract);
  and and_9 (and_9_out, XOR0, subtract);
  xor xor_18 (ADDSUB1, XOR1, or_9_out);
  and and_10 (and_10_out, XOR1, or_9_out);
  xor xor_19 (ADDSUB2, XOR2, or_10_out);
  and and_11 (and_11_out, XOR2, or_10_out);
  xor xor_20 (ADDSUB3, XOR3, or_11_out);
  and and_12 (and_12_out, XOR3, or_11_out);
  xor xor_21 (ADDSUB4, XOR4, or_12_out);
  and and_13 (and_13_out, XOR4, or_12_out);
  xor xor_22 (ADDSUB5, XOR5, or_13_out);
  and and_14 (and_14_out, XOR5, or_13_out);
  xor xor_23 (ADDSUB6, XOR6, or_14_out);
  and and_15 (and_15_out, XOR6, or_14_out);
  xor xor_24 (ADDSUB7, XOR7, or_15_out);
  and and_16 (and_16_out, XOR7, or_15_out);
  or or_9 (or_9_out, and_9_out, AND0);
  or or_10 (or_10_out, and_10_out, AND1);
  or or_11 (or_11_out, and_11_out, AND2);
  or or_12 (or_12_out, and_12_out, AND3);
  or or_13 (or_13_out, and_13_out, AND4);
  or or_14 (or_14_out, and_14_out, AND5);
  or or_15 (or_15_out, and_15_out, AND6);
  or or_16 (carry, and_16_out, AND7);

  assign SHL0 = 1'b0;
  assign SHL1 = b0;
  assign SHL2 = b1;
  assign SHL3 = b2;
  assign SHL4 = b3;
  assign SHL5 = b4;
  assign SHL6 = b5;
  assign SHL7 = b6;
  assign SHR0 = b1;
  assign SHR1 = b2;
  assign SHR2 = b3;
  assign SHR3 = b4;
  assign SHR4 = b5;
  assign SHR5 = b6;
  assign SHR6 = b7;
  assign SHR7 = 1'b0;
endmodule
