// Logisim project 4bit_carry_lookahead_adder.circ as structural Verilog: 1 circuit, main circuit main
module main (
  input  carry_in,
  input  a0,
  input  b0,
  input  a1,
  input  b1,
  input  a2,
  input  b2,
  input  a3,
  input  b3,
  output sum0,
  output sum1,
  output sum2,
  output sum3,
  output carry_out
);

  wire and_1_out, and_2_out, and_3_out, and_4_out, and_5_out, and_6_out, and_7_out, and_8_out, and_9_out,
       and_10_out, g0_out, g1_out, g2_out, g3_out, or_1_out, or_2_out, or_3_out, p0_out, p1_out, p2_out,
       p3_out;

  xor p0 (p0_out, a0, b0);
  and g0 (g0_out, a0, b0);
  xor p1 (p1_out, a1, b1);
  and g1 (g1_out, a1, b1);
  xor p2 (p2_out, a2, b2);
  and g2 (g2_out, a2, b2);
  xor p3 (p3_out, a3, b3);
  and g3 (g3_out, a3, b3);
  and and_1 (and_1_out, p0_out, carry_in);
  xor xor_1 (sum0, p0_out, carry_in);
  or or_1 (or_1_out, g0_out, and_1_out);
  and and_2 (and_2_out, p1_out, and_1_out);
  xor xor_2 (sum1, p1_out, or_1_out);
  and and_3 (and_3_out, p1_out, g0_out);
  and and_4 (and_4_out, p2_out, and_2_out);
  or or_2 (or_2_out, g1_out, and_3_out, and_2_out);
  and and_5 (and_5_out, p2_out, g1_out);
  and and_6 (and_6_out, p2_out, and_3_out);
  and and_7 (and_7_out, p3_out, and_6_out);
  and and_8 (and_8_out, p3_out, and_4_out);
  xor xor_3 (sum2, p2_out, or_2_out);
  or or_3 (or_3_out, g2_out, and_5_out, and_6_out, and_4_out);
  and and_9 (and_9_out, p3_out, g2_out);
  and and_10 (and_10_out, p3_out, and_5_out);
  xor xor_4 (sum3, p3_out, or_3_out);
  or or_4 (carry_out, g3_out, and_9_out, and_10_out, and_7_out, and_8_out);
endmodule
