// Logisim project carry_lookahead_adder.circ as structural Verilog: 1 circuit, main circuit main
module main (
  input  a,
  input  b,
  input  carry_in,
  output sum,
  output carry_propagator,
  output carry_generator
);

  wire xor_1_out;

  xor xor_1 (xor_1_out, a, b);
  and and_1 (carry_generator, a, b);
  xor xor_2 (sum, xor_1_out, carry_in);
  and and_2 (carry_propagator, xor_1_out, carry_in);
endmodule
