// Logisim project nand_gate.circ as structural Verilog: 1 circuit, main circuit main
module main (
  input  x,
  input  y,
  output x_nand_y
);

  wire transistor_2_out;

  Pull_Resistor #(.pull(1)) pull_resistor_1 (.node(x_nand_y));
  Transistor #(.\type ("n")) transistor_1 (.in(transistor_2_out), .out(x_nand_y), .gate(x));
  Transistor #(.\type ("n")) transistor_2 (.in(1'b0), .out(transistor_2_out), .gate(y));
endmodule
