// Logisim project D_Latch.circ as structural Verilog: 1 circuit, main circuit main
module main (
  input  D,
  input  EN,
  output Q
);

  wire and_1_out, and_2_out, nor_2_out, not_1_out;

  not not_1 (not_1_out, D);
  and and_1 (and_1_out, not_1_out, EN);
  and and_2 (and_2_out, EN, D);
  nor nor_1 (Q, and_1_out, nor_2_out);
  nor nor_2 (nor_2_out, Q, and_2_out);
endmodule
