// Logisim project not_gate.circ as structural Verilog: 1 circuit, main circuit main
module main (
  input  x,
  output not_x
);

  Pull_Resistor #(.pull(1)) pull_resistor_1 (.node(not_x));
  Transistor #(.\type ("n")) transistor_1 (.in(1'b0), .out(not_x), .gate(x));
endmodule
