// Logisim project three_way_parity_light_control.circ as structural Verilog: 1 circuit, main circuit main
module main (
  input  x,
  input  y,
  input  z
);

  wire g1_out, g2_out;

  xor g1 (g1_out, x, y);
  xor g2 (g2_out, g1_out, z);
  LED led_1 (.in(g2_out));
endmodule
