// Logisim project seven_segment_display.circ as structural Verilog: 1 circuit, main circuit main
module main (
  input  b0,
  input  b1,
  input  b2,
  input  b3
);

  wire a_out, and_1_out, and_2_out, and_3_out, and_4_out, and_5_out, and_6_out, and_7_out, and_8_out,
       and_9_out, and_10_out, b_out, c_out, d_out, e_out, f_out, g_out, not_1_out, not_2_out, not_3_out;

  not not_1 (not_1_out, b0);
  not not_2 (not_2_out, b1);
  not not_3 (not_3_out, b2);
  and and_1 (and_1_out, b0, b2);
  and and_2 (and_2_out, not_1_out, not_3_out);
  and and_3 (and_3_out, b1, not_3_out);
  and and_4 (and_4_out, not_2_out, b0, b2);
  and and_5 (and_5_out, b1, not_1_out);
  or a (a_out, and_1_out, and_2_out, b1, b3);
  and and_6 (and_6_out, b1, b0);
  and and_7 (and_7_out, not_2_out, not_1_out);
  and and_8 (and_8_out, not_2_out, b2);
  and and_9 (and_9_out, not_1_out, b2);
  or b (b_out, and_6_out, and_7_out, not_3_out);
  or c (c_out, not_2_out, b0, b2);
  or d (d_out, and_2_out, and_3_out, and_4_out, and_5_out, b3);
  and and_10 (and_10_out, not_2_out, b2);
  _7_Segment_Display u_7_segment_display_1 (
    .g(g_out), .f(f_out), .a(a_out), .b(b_out), .e(e_out), .d(d_out), .c(c_out));  // open: dp
  or e (e_out, and_2_out, and_5_out);
  or f (f_out, b3, and_7_out, and_8_out, and_9_out);
  or g (g_out, b3, and_5_out, and_10_out, and_3_out);
endmodule
