// Logisim project Serenity.circ as structural Verilog: 9 circuits, main circuit main
module main (
  input  in_1,
  input  in_2,
  input  in_3,
  input  in_4,
  input  in_5,
  input  in_6,
  input  in_7,
  input  in_8,
  input  in_9,
  input  in_10
);

  wire dflipflop_1_q, dflipflop_2_q, dflipflop_3_q, dflipflop_4_q, dflipflop_5_q, dflipflop_6_q,
       dflipflop_7_q, dflipflop_8_q, full4bitadditioncircuit_1_out_10, full4bitadditioncircuit_1_out_11,
       full4bitadditioncircuit_1_out_12, full4bitadditioncircuit_1_out_13, full4x4bitsram_1_b0,
       full4x4bitsram_1_b1, full4x4bitsram_1_b2, full4x4bitsram_1_b3;

  Full4x4bitsRAM full4x4bitsram_1 (
    .in_1(in_4), .in_2(in_5), .in_3(in_6), .in_4(in_7), .in_5(in_1), .Adr1(in_2), .Adr0(in_3),
    .b3(full4x4bitsram_1_b3), .b2(full4x4bitsram_1_b2), .b1(full4x4bitsram_1_b1), .b0(full4x4bitsram_1_b0));
  _7_Segment_Display u_7_segment_display_1 ();  // open: g, f, a, b, e, d, c, dp
  _7_Segment_Display u_7_segment_display_2 ();  // open: g, f, a, b, e, d, c, dp
  DFlipFlop dflipflop_1 (.D(in_4), .CLK(in_9), .Q(dflipflop_1_q));
  DFlipFlop dflipflop_2 (.D(in_5), .CLK(in_9), .Q(dflipflop_2_q));
  DFlipFlop dflipflop_3 (.D(in_6), .CLK(in_9), .Q(dflipflop_3_q));
  DFlipFlop dflipflop_4 (.D(in_7), .CLK(in_9), .Q(dflipflop_4_q));
  Full4BitAdditionCircuit full4bitadditioncircuit_1 (
    .A3(dflipflop_1_q), .in_2(dflipflop_5_q), .A2(dflipflop_2_q), .B2(dflipflop_6_q), .A1(dflipflop_3_q),
    .in_6(dflipflop_7_q), .in_7(dflipflop_4_q), .in_8(dflipflop_8_q), .in_9(in_8),
    .out_10(full4bitadditioncircuit_1_out_10), .out_11(full4bitadditioncircuit_1_out_11),
    .out_12(full4bitadditioncircuit_1_out_12), .out_13(full4bitadditioncircuit_1_out_13));
  DFlipFlop dflipflop_5 (.D(in_4), .CLK(in_10), .Q(dflipflop_5_q));
  DFlipFlop dflipflop_6 (.D(in_5), .CLK(in_10), .Q(dflipflop_6_q));
  DFlipFlop dflipflop_7 (.D(in_6), .CLK(in_10), .Q(dflipflop_7_q));
  DFlipFlop dflipflop_8 (.D(in_7), .CLK(in_10), .Q(dflipflop_8_q));

  // Notes on the sheet:
  //   Write RAM
  //   bAdr1
  //   bAdr0
  //   b3
  //   b1
  //   b2
  //   b0
  //   Write A
  //   Write B
endmodule

module Full4BitAdditionCircuit (
  input  A3,
  input  in_2,
  input  A2,
  input  B2,
  input  A1,
  input  in_6,
  input  in_7,
  input  in_8,
  input  in_9,
  output out_10,
  output out_11,
  output out_12,
  output out_13
);

  wire fulladder_2_cout, fulladder_3_cout, fulladder_4_cout, xor_1_out, xor_2_out, xor_3_out, xor_4_out;

  xor xor_1 (xor_1_out, in_2, in_9);
  FullAdder fulladder_1 (.B(xor_1_out), .Cin(fulladder_2_cout), .A(A3), .Sum(out_10));  // open: Cout
  xor xor_2 (xor_2_out, B2, in_9);
  FullAdder fulladder_2 (.B(xor_2_out), .Cin(fulladder_3_cout), .A(A2), .Sum(out_11), .Cout(fulladder_2_cout));
  xor xor_3 (xor_3_out, in_6, in_9);
  FullAdder fulladder_3 (.B(xor_3_out), .Cin(fulladder_4_cout), .A(A1), .Sum(out_12), .Cout(fulladder_3_cout));
  xor xor_4 (xor_4_out, in_8, in_9);
  FullAdder fulladder_4 (.B(xor_4_out), .Cin(in_9), .A(in_7), .Sum(out_13), .Cout(fulladder_4_cout));

  // Notes on the sheet:
  //   B3
  //   S3
  //   S2
  //   B1
  //   S1
  //   A0
  //   B0
  //   S0
endmodule

module Full4x4bitsRAM (
  input  in_1,
  input  in_2,
  input  in_3,
  input  in_4,
  input  in_5,
  input  Adr1,
  input  Adr0,
  output b3,
  output b2,
  output b1,
  output b0
);

  wire and_1_out, and_2_out, and_3_out, and_4_out, and_5_out, and_6_out, and_7_out, and_8_out, and_9_out,
       and_10_out, and_11_out, and_12_out, and_13_out, and_14_out, and_15_out, and_16_out, and_17_out,
       and_18_out, and_19_out, and_20_out, and_21_out, and_22_out, and_23_out, and_24_out, dflipflop_1_q,
       dflipflop_2_q, dflipflop_3_q, dflipflop_4_q, dflipflop_5_q, dflipflop_6_q, dflipflop_7_q,
       dflipflop_8_q, dflipflop_9_q, dflipflop_10_q, dflipflop_11_q, dflipflop_12_q, dflipflop_13_q,
       dflipflop_14_q, dflipflop_15_q, dflipflop_16_q, not_1_out, not_2_out, not_3_out, not_4_out, or_1_out,
       or_2_out, or_3_out, or_4_out, or_5_out, or_6_out, or_7_out, or_8_out;

  not not_1 (not_1_out, Adr1);
  not not_2 (not_2_out, Adr0);
  not not_3 (not_3_out, Adr1);
  not not_4 (not_4_out, Adr0);
  and and_1 (and_1_out, not_1_out, not_2_out);
  and and_2 (and_2_out, not_3_out, Adr0);
  and and_3 (and_3_out, Adr1, not_4_out);
  and and_4 (and_4_out, Adr1, Adr0);
  and and_5 (and_5_out, and_1_out, in_5);
  and and_6 (and_6_out, and_2_out, in_5);
  and and_7 (and_7_out, and_3_out, in_5);
  and and_8 (and_8_out, and_4_out, in_5);
  DFlipFlop dflipflop_1 (.D(in_1), .CLK(and_5_out), .Q(dflipflop_1_q));
  DFlipFlop dflipflop_2 (.D(in_2), .CLK(and_5_out), .Q(dflipflop_2_q));
  DFlipFlop dflipflop_3 (.D(in_3), .CLK(and_5_out), .Q(dflipflop_3_q));
  DFlipFlop dflipflop_4 (.D(in_4), .CLK(and_5_out), .Q(dflipflop_4_q));
  DFlipFlop dflipflop_5 (.D(in_1), .CLK(and_6_out), .Q(dflipflop_5_q));
  DFlipFlop dflipflop_6 (.D(in_2), .CLK(and_6_out), .Q(dflipflop_6_q));
  DFlipFlop dflipflop_7 (.D(in_3), .CLK(and_6_out), .Q(dflipflop_7_q));
  DFlipFlop dflipflop_8 (.D(in_4), .CLK(and_6_out), .Q(dflipflop_8_q));
  DFlipFlop dflipflop_9 (.D(in_1), .CLK(and_7_out), .Q(dflipflop_9_q));
  DFlipFlop dflipflop_10 (.D(in_2), .CLK(and_7_out), .Q(dflipflop_10_q));
  DFlipFlop dflipflop_11 (.D(in_3), .CLK(and_7_out), .Q(dflipflop_11_q));
  DFlipFlop dflipflop_12 (.D(in_4), .CLK(and_7_out), .Q(dflipflop_12_q));
  DFlipFlop dflipflop_13 (.D(in_1), .CLK(and_8_out), .Q(dflipflop_13_q));
  DFlipFlop dflipflop_14 (.D(in_2), .CLK(and_8_out), .Q(dflipflop_14_q));
  DFlipFlop dflipflop_15 (.D(in_3), .CLK(and_8_out), .Q(dflipflop_15_q));
  DFlipFlop dflipflop_16 (.D(in_4), .CLK(and_8_out), .Q(dflipflop_16_q));
  and and_9 (and_9_out, and_1_out, dflipflop_1_q);
  and and_10 (and_10_out, and_1_out, dflipflop_2_q);
  and and_11 (and_11_out, and_1_out, dflipflop_3_q);
  and and_12 (and_12_out, and_1_out, dflipflop_4_q);
  and and_13 (and_13_out, and_2_out, dflipflop_5_q);
  and and_14 (and_14_out, and_2_out, dflipflop_6_q);
  and and_15 (and_15_out, and_2_out, dflipflop_7_q);
  and and_16 (and_16_out, and_2_out, dflipflop_8_q);
  and and_17 (and_17_out, and_3_out, dflipflop_9_q);
  and and_18 (and_18_out, and_3_out, dflipflop_10_q);
  and and_19 (and_19_out, and_3_out, dflipflop_11_q);
  and and_20 (and_20_out, and_3_out, dflipflop_12_q);
  and and_21 (and_21_out, and_4_out, dflipflop_13_q);
  and and_22 (and_22_out, and_4_out, dflipflop_14_q);
  and and_23 (and_23_out, and_4_out, dflipflop_15_q);
  and and_24 (and_24_out, and_4_out, dflipflop_16_q);
  or or_1 (or_1_out, and_9_out, and_13_out);
  or or_2 (or_2_out, and_10_out, and_14_out);
  or or_3 (or_3_out, and_11_out, and_15_out);
  or or_4 (or_4_out, and_12_out, and_16_out);
  or or_5 (or_5_out, and_17_out, and_21_out);
  or or_6 (or_6_out, and_18_out, and_22_out);
  or or_7 (or_7_out, and_19_out, and_23_out);
  or or_8 (or_8_out, and_20_out, and_24_out);
  or or_9 (b3, or_1_out, or_5_out);
  or or_10 (b2, or_2_out, or_6_out);
  or or_11 (b1, or_3_out, or_7_out);
  or or_12 (b0, or_4_out, or_8_out);

  // Notes on the sheet:
  //   b2
  //   b3
  //   b1
  //   b0
  //   Write
endmodule

module Full4BitAdditionCircuitWithOutputRegisters (
  input  in_1,
  input  A3,
  input  B3,
  input  A2,
  input  B2,
  input  A1,
  input  B1,
  input  A0,
  input  B0,
  input  CLK,
  output out_11,
  output out_12,
  output out_13,
  output out_14
);

  wire full4bitadditioncircuit_1_out_10, full4bitadditioncircuit_1_out_11, full4bitadditioncircuit_1_out_12,
       full4bitadditioncircuit_1_out_13;

  DFlipFlop dflipflop_1 (.D(full4bitadditioncircuit_1_out_10), .CLK(CLK), .Q(out_11));
  DFlipFlop dflipflop_2 (.D(full4bitadditioncircuit_1_out_11), .CLK(CLK), .Q(out_12));
  DFlipFlop dflipflop_3 (.D(full4bitadditioncircuit_1_out_12), .CLK(CLK), .Q(out_13));
  DFlipFlop dflipflop_4 (.D(full4bitadditioncircuit_1_out_13), .CLK(CLK), .Q(out_14));
  Full4BitAdditionCircuit full4bitadditioncircuit_1 (
    .A3(A3), .in_2(B3), .A2(A2), .B2(B2), .A1(A1), .in_6(B1), .in_7(A0), .in_8(B0), .in_9(in_1),
    .out_10(full4bitadditioncircuit_1_out_10), .out_11(full4bitadditioncircuit_1_out_11),
    .out_12(full4bitadditioncircuit_1_out_12), .out_13(full4bitadditioncircuit_1_out_13));

  // Notes on the sheet:
  //   S3
  //   S2
  //   S1
  //   S0
endmodule

module Full4BitCounter (
  input  in_1,
  input  A3,
  input  A2,
  input  A1,
  input  A0,
  input  in_6,
  output out_7,
  output out_8,
  output out_9,
  output out_10
);

  wire full4bitadditioncircuit_1_out_10, full4bitadditioncircuit_1_out_11, full4bitadditioncircuit_1_out_12,
       full4bitadditioncircuit_1_out_13;

  DFlipFlop dflipflop_1 (.D(full4bitadditioncircuit_1_out_10), .CLK(in_6), .Q(out_7));
  DFlipFlop dflipflop_2 (.D(full4bitadditioncircuit_1_out_11), .CLK(in_6), .Q(out_8));
  DFlipFlop dflipflop_3 (.D(full4bitadditioncircuit_1_out_12), .CLK(in_6), .Q(out_9));
  DFlipFlop dflipflop_4 (.D(full4bitadditioncircuit_1_out_13), .CLK(in_6), .Q(out_10));
  Full4BitAdditionCircuit full4bitadditioncircuit_1 (
    .A3(A3), .in_2(out_7), .A2(A2), .B2(out_8), .A1(A1), .in_6(out_9), .in_7(A0), .in_8(out_10), .in_9(in_1),
    .out_10(full4bitadditioncircuit_1_out_10), .out_11(full4bitadditioncircuit_1_out_11),
    .out_12(full4bitadditioncircuit_1_out_12), .out_13(full4bitadditioncircuit_1_out_13));

  // Notes on the sheet:
  //   S3
  //   S2
  //   S1
  //   S0
  //   B3
  //   B2
  //   B1
  //   B0
endmodule

module DFlipFlop (
  input  D,
  input  CLK,
  output Q
);

  D_Flip_Flop d_ff_1 (.D(D), .clk(CLK), .Q(Q));  // open: Qn, preset, reset
endmodule

module FullAdder (
  input  A,
  input  B,
  input  Cin,
  output Sum,
  output Cout
);

  wire and_1_out, and_2_out, or_1_out, xor_1_out;

  and and_1 (and_1_out, A, B);
  or or_1 (or_1_out, A, B);
  xor xor_1 (xor_1_out, A, B);
  and and_2 (and_2_out, or_1_out, Cin);
  xor xor_2 (Sum, xor_1_out, Cin);
  or or_2 (Cout, and_1_out, and_2_out);
endmodule

module DLatch (
  input  En,
  input  D,
  output Q,
  output nQ
);

  wire and_1_out, and_2_out, not_1_out;

  not not_1 (not_1_out, D);
  and and_1 (and_1_out, not_1_out, En);
  and and_2 (and_2_out, En, D);
  RSLatch rslatch_1 (.R(and_1_out), .S(and_2_out), .Q(Q), .nQ(nQ));
endmodule

module RSLatch (
  input  R,
  input  S,
  output Q,
  output nQ
);

  nor nor_1 (Q, R, nQ);
  nor nor_2 (nQ, Q, S);
endmodule
